// Logisim project CPU.circ as structural Verilog
// REG
module Registrador (
  input  [3:0] RsX,
  input  [3:0] RsY,
  input  [3:0] Rd,
  input  [7:0] Rin,
  input  rwctl,
  output [7:0] R0,
  output [7:0] Rx,
  output [7:0] Ry
);

  wire comparator_1_eq, demultiplexer_1_out1, demultiplexer_1_out2, demultiplexer_1_out3,
       demultiplexer_1_out4, demultiplexer_1_out5, demultiplexer_1_out6, demultiplexer_1_out7,
       demultiplexer_1_out8, demultiplexer_1_out9, demultiplexer_1_out10, demultiplexer_1_out11,
       demultiplexer_1_out12, demultiplexer_1_out13, demultiplexer_1_out14, demultiplexer_1_out15, not_1_out,
       not_2_out, undriven;
  wire [7:0] register_1_q, register_2_q, register_3_q, register_4_q, register_5_q, register_6_q,
       register_7_q, register_8_q, register_9_q, register_10_q, register_11_q, register_12_q, register_13_q,
       register_14_q, register_15_q;

  not not_1 (not_1_out, rwctl);
  Demultiplexer #(.select(4), .enable("false")) demultiplexer_1 (
    .out1(demultiplexer_1_out1), .out2(demultiplexer_1_out2), .out3(demultiplexer_1_out3),
    .out4(demultiplexer_1_out4), .out5(demultiplexer_1_out5), .out6(demultiplexer_1_out6),
    .out7(demultiplexer_1_out7), .out8(demultiplexer_1_out8), .out9(demultiplexer_1_out9),
    .out10(demultiplexer_1_out10), .out11(demultiplexer_1_out11), .out12(demultiplexer_1_out12),
    .out13(demultiplexer_1_out13), .out14(demultiplexer_1_out14), .out15(demultiplexer_1_out15),
    .in(not_1_out), .sel(Rd));  // open: out0
  not not_2 (not_2_out, comparator_1_eq);
  Comparator comparator_1 (.a({8{1'b0}}), .b(Rin), .eq(comparator_1_eq));  // open: gt, lt
  assign R0 = {{7{1'b0}}, not_2_out};  // Bit_Extender bit_extender_1
  Register register_1 (.D(Rin), .Q(register_1_q), .clk(demultiplexer_1_out1));  // open: en, clr
  Register register_2 (.D(Rin), .Q(register_2_q), .clk(demultiplexer_1_out2));  // open: en, clr
  Register register_3 (.D(Rin), .Q(register_3_q), .clk(demultiplexer_1_out3));  // open: en, clr
  Register register_4 (.D(Rin), .Q(register_4_q), .clk(demultiplexer_1_out4));  // open: en, clr
  Register register_5 (.D(Rin), .Q(register_5_q), .clk(demultiplexer_1_out5));  // open: en, clr
  Register register_6 (.D(Rin), .Q(register_6_q), .clk(demultiplexer_1_out6));  // open: en, clr
  Register register_7 (.D(Rin), .Q(register_7_q), .clk(demultiplexer_1_out7));  // open: en, clr
  Register register_8 (.D(Rin), .en(undriven), .Q(register_8_q), .clk(demultiplexer_1_out8));  // open: clr
  Register register_9 (.D(Rin), .Q(register_9_q), .clk(demultiplexer_1_out9));  // open: en, clr
  Register register_10 (.D(Rin), .Q(register_10_q), .clk(demultiplexer_1_out10));  // open: en, clr
  Register register_11 (.D(Rin), .Q(register_11_q), .clk(demultiplexer_1_out11));  // open: en, clr
  Register register_12 (.D(Rin), .Q(register_12_q), .clk(demultiplexer_1_out12));  // open: en, clr
  Register register_13 (.D(Rin), .Q(register_13_q), .clk(demultiplexer_1_out13));  // open: en, clr
  Register register_14 (.D(Rin), .Q(register_14_q), .clk(demultiplexer_1_out14));  // open: en, clr
  Register register_15 (.D(Rin), .Q(register_15_q), .clk(demultiplexer_1_out15));  // open: en, clr
  Multiplexer #(.select(4), .width(8), .enable("false")) multiplexer_1 (
    .in0(R0), .in1(register_1_q), .in2(register_2_q), .in3(register_3_q), .in4(register_4_q),
    .in5(register_5_q), .in6(register_6_q), .in7(register_7_q), .in8(register_8_q), .in9(register_9_q),
    .in10(register_10_q), .in11(register_11_q), .in12(register_12_q), .in13(register_13_q),
    .in14(register_14_q), .in15(register_15_q), .out(Rx), .sel(RsX));
  Multiplexer #(.select(4), .width(8), .enable("false")) multiplexer_2 (
    .in0(R0), .in1(register_1_q), .in2(register_2_q), .in3(register_3_q), .in4(register_4_q),
    .in5(register_5_q), .in6(register_6_q), .in7(register_7_q), .in8(register_8_q), .in9(register_9_q),
    .in10(register_10_q), .in11(register_11_q), .in12(register_12_q), .in13(register_13_q),
    .in14(register_14_q), .in15(register_15_q), .out(Ry), .sel(RsY));

  // Other names for the same wires on the sheet: Rs1[3:0] = RsX; Rs2[3:0] = RsY
endmodule

// ULA
module \Unidade_Lógica_Aritimética  (
  input  [7:0] Ix,
  input  [7:0] Iy,
  input  [3:0] Op,
  output [7:0] Out
);

  wire comparator_1_eq, comparator_2_eq, comparator_3_lt, comparator_4_eq, comparator_4_lt, or_2_out;
  wire [7:0] adder_1_out, and_1_out, bit_extender_1_out, bit_extender_2_out, bit_extender_3_out,
       bit_extender_4_out, divider_1_out, multiplier_1_out, or_1_out, subtractor_1_out;

  assign and_1_out = Ix & Iy;  // AND_Gate and_1, 8 bits wide
  assign or_1_out = Ix | Iy;  // OR_Gate or_1, 8 bits wide
  Comparator comparator_1 (.a({8{1'b0}}), .b(Iy), .eq(comparator_1_eq));  // open: gt, lt
  Adder adder_1 (.a(Ix), .b(Iy), .out(adder_1_out));  // open: cin, cout
  Subtractor subtractor_1 (.a(Ix), .b(Iy), .out(subtractor_1_out));  // open: bin, bout
  Multiplier multiplier_1 (.a(Ix), .b(Iy), .out(multiplier_1_out));  // open: cin, cout
  Divider divider_1 (.a(Ix), .b(Iy), .out(divider_1_out));  // open: upper, rem
  Comparator comparator_2 (.a(Ix), .b(Iy), .eq(comparator_2_eq));  // open: gt, lt
  Comparator comparator_3 (.a(Ix), .b(Iy), .lt(comparator_3_lt));  // open: gt, eq
  Comparator comparator_4 (.a(Ix), .b(Iy), .eq(comparator_4_eq), .lt(comparator_4_lt));  // open: gt
  assign bit_extender_1_out = {{7{1'b0}}, comparator_1_eq};  // Bit_Extender bit_extender_1
  or or_2 (or_2_out, comparator_4_eq, comparator_4_lt);
  assign bit_extender_2_out = {{7{1'b0}}, comparator_2_eq};  // Bit_Extender bit_extender_2
  assign bit_extender_3_out = {{7{1'b0}}, comparator_3_lt};  // Bit_Extender bit_extender_3
  assign bit_extender_4_out = {{7{1'b0}}, or_2_out};  // Bit_Extender bit_extender_4
  Multiplexer #(.select(4), .width(8), .enable("false")) multiplexer_1 (
    .in0(and_1_out), .in1(or_1_out), .in2(bit_extender_1_out), .in3(adder_1_out), .in4(subtractor_1_out),
    .in5(multiplier_1_out), .in6(divider_1_out), .in7(bit_extender_2_out), .in8(bit_extender_3_out),
    .in9(bit_extender_4_out), .out(Out), .sel(Op));  // open: in10, in11, in12, in13, in14, in15
endmodule

module REG_ULA (
  input  [3:0] RsX,
  input  [7:0] Ix,
  input  [3:0] RsY,
  input  [7:0] Iy,
  input  [3:0] Rd,
  input  [3:0] Op_ULA,
  input  rwctl,
  input  [2:0] rinctl,
  output [7:0] R0,
  output [7:0] Out_ULA,
  output [7:0] Rx,
  output [7:0] Ry
);

  wire [7:0] IR, \Memória , OUT_rinctl, PC;

  Registrador registrador_1 (.RsX(RsX), .RsY(RsY), .Rd(Rd), .Rin(OUT_rinctl), .rwctl(rwctl), .R0(R0), .Rx(Rx), .Ry(Ry));
  \Unidade_Lógica_Aritimética  \unidade_lógica_aritimética_1  (.Ix(Ix), .Iy(Iy), .Op(Op_ULA), .Out(Out_ULA));
  Multiplexer #(.select(3), .width(8), .enable("false")) multiplexer_1 (
    .in0(Out_ULA), .in1(\Memória ), .in2(IR), .in3(OUT_rinctl), .in4(PC), .out(OUT_rinctl), .sel(rinctl));  // open: in5, in6, in7

  // Other names for the same wires on the sheet: Op[3:0] = Op_ULA; Rin[7:0] = OUT_rinctl

  // Notes on the sheet:
  //   ENTRADAS E SAÍDAS SEPARADAS ULA
  //   ENTRADAS E SAÍDAS SEPARADAS REG
endmodule

module IDEC (
  input  [11:0] \INSTRUÇÃO ,
  input  [2:0] AND,
  input  [2:0] OR,
  input  [2:0] ADD,
  input  [2:0] SUB,
  input  [2:0] MUL,
  input  [2:0] DIV,
  input  [2:0] EQ,
  input  [2:0] LT,
  input  [2:0] LEQ,
  input  [2:0] NOT,
  input  [2:0] MOV,
  input  [2:0] LDA,
  input  [2:0] STR,
  input  [2:0] JMP,
  input  [2:0] HLT,
  input  [2:0] LDI,
  output [3:0] \Cód_OP ,
  output [3:0] MEIO,
  output ALU_MOV,
  output [3:0] MENOR,
  output NOT_2,
  output LDA_STR_JMP,
  output LDI_2,
  output HLT_2
);

  wire [2:0] teste;
  wire [7:0] bit_extender_1_out, bit_extender_2_out, bit_extender_3_out, bit_extender_4_out,
       bit_extender_5_out;

  Multiplexer #(.select(4), .width(3), .enable("false")) multiplexer_1 (
    .in0(AND), .in1(OR), .in2(NOT), .in3(ADD), .in4(SUB), .in5(MUL), .in6(DIV), .in7(EQ), .in8(LT),
    .in9(LEQ), .in10(LDA), .in11(LDI), .in12(STR), .in13(MOV), .in14(JMP), .in15(HLT), .out(teste),
    .sel(\INSTRUÇÃO [11:8]));
  assign bit_extender_1_out = {{5{1'b0}}, teste};  // Bit_Extender bit_extender_1
  assign bit_extender_2_out = {{5{1'b0}}, teste};  // Bit_Extender bit_extender_2
  assign bit_extender_3_out = {{5{1'b0}}, teste};  // Bit_Extender bit_extender_3
  assign bit_extender_4_out = {{5{1'b0}}, teste};  // Bit_Extender bit_extender_4
  assign bit_extender_5_out = {{5{1'b0}}, teste};  // Bit_Extender bit_extender_5
  Comparator comparator_1 (.a({8{1'b0}}), .b(bit_extender_1_out), .eq(ALU_MOV));  // open: gt, lt
  Comparator comparator_2 (.a(8'h1), .b(bit_extender_2_out), .eq(NOT_2));  // open: gt, lt
  Comparator comparator_3 (.a(8'h2), .b(bit_extender_3_out), .eq(LDA_STR_JMP));  // open: gt, lt
  Comparator comparator_4 (.a(8'h3), .b(bit_extender_4_out), .eq(LDI_2));  // open: gt, lt
  Comparator comparator_5 (.a(8'h4), .b(bit_extender_5_out), .eq(HLT_2));  // open: gt, lt

  assign \Cód_OP  = \INSTRUÇÃO [11:8];
  assign MEIO = \INSTRUÇÃO [7:4];
  assign MENOR = \INSTRUÇÃO [3:0];

  // Other names for the same wires on the sheet: Cod_Op[3:0] = \INSTRUÇÃO [11:8]
endmodule
